# Fritzing sketch gaydar_schematic (saved by Fritzing 0.9.3b)
breadboards: 1

parts:
  Part1 = Arduino Uno (Rev3)
  R1 = Resistor [tolerance=±5% resistance=220 package=THT]
  R2 = Resistor [tolerance=±5% resistance=220 package=THT]
  LED1 = LED - 5mm [color="Red (633nm)" package="5 mm [THT]"]
  LED2 = LED - 5mm [color="Red (633nm)" package="5 mm [THT]"]
  LED3 = LED - 5mm [color="Red (633nm)" package="5 mm [THT]"]
  R3 = Resistor [tolerance=±5% resistance=220 package=THT]
  R4 = Resistor [tolerance=±5% resistance=220 package=THT]
  LED4 = LED - 5mm [color="Yellow (585nm)" package="5 mm [THT]"]
  LED5 = LED - 5mm [color="Yellow (585nm)" package="5 mm [THT]"]
  LED6 = LED - 5mm [color="Yellow (585nm)" package="5 mm [THT]"]
  LED7 = LED - 5mm [color="Yellow (585nm)" package="5 mm [THT]"]
  R5 = Resistor [tolerance=±5% resistance=220 package=THT]
  R6 = Resistor [tolerance=±5% resistance=220 package=THT]
  R7 = Resistor [tolerance=±5% resistance=220 package=THT]
  R8 = Resistor [tolerance=±5% resistance=220 package=THT]
  LED8 = LED - 5mm [color="Green (555nm)" package="5 mm [THT]"]
  LED9 = LED - 5mm [color="Green (555nm)" package="5 mm [THT]"]
  LED10 = LED - 5mm [color="Green (555nm)" package="5 mm [THT]"]
  R9 = Resistor [tolerance=±5% resistance=220 package=THT]
  R10 = Resistor [tolerance=±5% resistance=220 package=THT]
  LED11 = LED - 5mm [color="Blue (430nm)" package="5 mm [THT]"]
  R11 = Resistor [tolerance=±5% resistance=220 package=THT]
  S1 = Pushbutton [package="[THT]"]
  R12 = Resistor [tolerance=±5% resistance=10k package=THT]

nets:
  N1: Part1.D8, LED6.anode
  N2: Part1.D9_PWM, LED7.anode
  N3: Part1.D10_PWM/SS, LED8.anode
  N4: Part1.D11_PWM/MOSI, LED9.anode
  N5: Part1.D12/MISO, LED10.anode
  N6: Part1.D13/SCK, LED11.anode
  N7: Part1.GND, R1.Pin_1, R2.Pin_1, R3.Pin_1, R4.Pin_1, R5.Pin_1, R6.Pin_1, R7.Pin_1, R8.Pin_1, R9.Pin_1, R10.Pin_1, R11.Pin_1, S1.Pin_3, S1.Pin_4
  N8: Part1.D2, S1.Pin_1, S1.Pin_2, R12.Pin_1
  N9: Part1.D3_PWM, LED1.anode
  N10: Part1.D4, LED2.anode
  N11: Part1.D5_PWM, LED3.anode
  N12: Part1.D6_PWM, LED4.anode
  N13: Part1.D7, LED5.anode
  N14: Part1.5V, R12.Pin_0
  N15: R1.Pin_0, LED2.cathode
  N16: R2.Pin_0, LED1.cathode
  N17: LED3.cathode, R3.Pin_0
  N18: R4.Pin_0, LED4.cathode
  N19: LED5.cathode, R5.Pin_0
  N20: LED6.cathode, R6.Pin_0
  N21: LED7.cathode, R7.Pin_0
  N22: R8.Pin_0, LED8.cathode
  N23: LED9.cathode, R9.Pin_0
  N24: LED10.cathode, R10.Pin_0
  N25: LED11.cathode, R11.Pin_0
